// Logisim project BeEight.circ as structural Verilog: 1 circuit, main circuit main
module main (
  input  Device0,
  input  in_2,
  input  Device1,
  input  in_4,
  input  Device2,
  input  in_6,
  input  Device3
);

  wire adder_2_cout, and_1_out, and_2_out, and_3_out, and_4_out, and_5_out, and_7_out, and_9_out, and_10_out,
       and_11_out, and_14_out, and_15_out, Carry, CLK, CLKIN, comparator_1_eq, comparator_1_lt,
       ConditionalFlag, ConditionalResult, controlled_buffer_13_out, controlled_buffer_15_out,
       controlled_buffer_16_out, controlled_buffer_17_out, controlled_buffer_18_out,
       controlled_buffer_19_out, controlled_buffer_20_out, controlled_buffer_21_out,
       controlled_buffer_22_out, Equal, GreaterThan, ia, ialu, im, ipb, ipc, ipcs, isb, LessThan,
       n74138_1_pin4, n74138_1_pin5, n74138_1_pin6, n74138_1_pin7, n74138_1_pin9, n74138_1_pin10,
       n74138_1_pin11, n74138_1_pin12, n74138_1_pin13, n74138_1_pin14, n74138_1_pin15, nor_1_out, not_1_out,
       not_2_out, not_3_out, not_4_out, not_5_out, not_6_out, not_7_out, not_8_out, not_9_out, not_10_out,
       not_11_out, not_12_out, not_13_out, not_15_out, not_16_out, not_17_out, not_18_out, not_19_out,
       not_20_out, nxt, oa, oalu, om, opb, opc, opcs, or_1_out, or_2_out, or_3_out, or_4_out, osb,
       pull_resistor_2_node, pull_resistor_3_node, pull_resistor_4_node, s_r_ff_1_qn, special, ucf;
  wire [3:0] Condition, controlled_buffer_4_out, Instruction, InstructionCounter, pull_resistor_1_node;
  wire [6:0] rom_1_data;
  wire [7:0] Accumulator, adder_1_out, adder_2_out, ALU, ALUin, Databus, multireg_1_out_7, multireg_1_out_8,
       multireg_1_out_9, multireg_1_out_10, multireg_1_out_11, multireg_1_out_12, multireg_1_out_13,
       multireg_1_out_14, multireg_1_out_15, multireg_1_out_16, multireg_1_out_17, multireg_1_out_18,
       multireg_1_out_19, multireg_1_out_20, multireg_1_out_21, multireg_1_out_22, multireg_1_out_23,
       multireg_1_out_24, multireg_1_out_25, multireg_1_out_26, multireg_1_out_27, multireg_1_out_28,
       multireg_1_out_29, multireg_1_out_30, multireg_1_out_31, multireg_1_out_32, multireg_1_out_33,
       multireg_1_out_34, multireg_1_out_35, multireg_1_out_36, multireg_1_out_37, multireg_1_out_38,
       nand_1_out, not_14_out, SecondaryBuffer;
  wire [7:4] ProgramCounterStorageUpper_q;
  wire [11:0] Address, StoredAddress, subtractor_1_out;
  wire [11:8] Databus12;

  Hex_Digit_Display #(.decimalPoint("false")) hex_digit_display_1 (.value(Instruction));
  Pull_Resistor pull_resistor_1 (.node(pull_resistor_1_node));
  and and_1 (and_1_out, osb, Instruction[0], Instruction[1], Instruction[2]);
  Hex_Digit_Display #(.decimalPoint("false")) hex_digit_display_2 (.value(Address[11:8]));
  Hex_Digit_Display #(.decimalPoint("false")) hex_digit_display_3 (.value(Address[7:4]));
  Hex_Digit_Display #(.decimalPoint("false")) hex_digit_display_4 (.value(InstructionCounter));
  not not_1 (not_1_out, and_1_out);
  and and_2 (and_2_out, and_1_out, ConditionalFlag);
  Hex_Digit_Display #(.decimalPoint("false")) hex_digit_display_5 (.value(Address[3:0]));
  Hex_Digit_Display #(.decimalPoint("false")) hex_digit_display_6 (.value(Databus12));
  Hex_Digit_Display #(.decimalPoint("false")) hex_digit_display_7 (.value(Databus[7:4]));
  Register ProgramCounterStorageLower (.D(Databus), .en(ipcs), .clk(CLK), .Q(StoredAddress[7:0]), .clr(in_2));
  Register ProgramCounterStorageUpper (
    .D({pull_resistor_1_node, Databus12}), .en(ipcs), .clk(CLK),
    .Q({ProgramCounterStorageUpper_q, StoredAddress[11:8]}), .clr(in_2));
  or or_1 (or_1_out, not_1_out, and_2_out);
  Hex_Digit_Display #(.decimalPoint("false")) hex_digit_display_8 (.value(Accumulator[7:4]));
  Hex_Digit_Display #(.decimalPoint("false")) hex_digit_display_9 (.value(Accumulator[3:0]));
  Hex_Digit_Display #(.decimalPoint("false")) hex_digit_display_10 (.value(Databus[3:0]));
  Hex_Digit_Display #(.decimalPoint("false")) hex_digit_display_11 (.value(Instruction));
  Clock clock_1 (.out(CLKIN));
  RAM #(.addrWidth(12), .databus("bidir"), .trigger("high"), .\type ("nonvolatile")) ram_1 (
    .addr(Address), .we(im), .oe(om), .data(Databus));
  Pull_Resistor pull_resistor_2 (.node(pull_resistor_2_node));
  Subtractor #(.width(12)) subtractor_1 (
    .a(Address), .b(12'h2), .out(subtractor_1_out), .bin(pull_resistor_2_node));  // open: bout
  and and_3 (and_3_out, opcs, special);
  and and_4 (and_4_out, CLK, or_1_out, ipc);
  Hex_Digit_Display #(.decimalPoint("false")) hex_digit_display_12 (.value(ALU[7:4]));
  Hex_Digit_Display #(.decimalPoint("false")) hex_digit_display_13 (.value(ALU[3:0]));
  Hex_Digit_Display #(.decimalPoint("false")) hex_digit_display_14 (.value(Condition));
  Hex_Digit_Display #(.decimalPoint("false")) hex_digit_display_15 (.value(SecondaryBuffer[7:4]));
  // Probe on subtractor_1_out[4:0]
  Comparator #(.mode("unsigned"), .width(7)) comparator_1 (
    .a(subtractor_1_out[11:5]), .b({7{1'b0}}), .eq(comparator_1_eq), .lt(comparator_1_lt));  // open: gt
  assign {Databus12, Databus} = and_5_out ? StoredAddress : 12'bz;  // Controlled_Buffer controlled_buffer_1
  and and_5 (and_5_out, opcs, not_2_out);
  not not_2 (not_2_out, special);
  assign Databus = and_3_out ? {ProgramCounterStorageUpper_q, StoredAddress[11:8]} : 8'bz;  // Controlled_Buffer controlled_buffer_2
  Counter #(.max('hfff), .width(12)) ProgramCounter (
    .clr(in_2), .load(not_3_out), .up(1'b1), .count(special), .clk(and_4_out), .D({Databus12, Databus}),
    .Q(Address));  // open: carry
  not not_3 (not_3_out, special);
  LED led_1 (.in(om));
  LED led_2 (.in(im));
  Hex_Digit_Display #(.decimalPoint("false")) hex_digit_display_16 (.value(SecondaryBuffer[3:0]));
  LED led_3 (.in(opb));
  LED led_4 (.in(osb));
  LED led_5 (.in(ipb));
  LED led_6 (.in(isb));
  Hex_Digit_Display #(.decimalPoint("false")) hex_digit_display_17 (.value(StoredAddress[11:8]));
  Hex_Digit_Display #(.decimalPoint("false")) hex_digit_display_18 (.value(StoredAddress[7:4]));
  or or_2 (or_2_out, comparator_1_eq, comparator_1_lt);
  LED led_7 (.in(oa));
  LED led_8 (.in(oalu));
  LED led_9 (.in(ia));
  LED led_10 (.in(ialu));
  Hex_Digit_Display #(.decimalPoint("false")) hex_digit_display_19 (.value(StoredAddress[3:0]));
  assign {Databus12, Databus} = opc ? Address : 12'bz;  // Controlled_Buffer controlled_buffer_3
  LED led_11 (.in(opc));
  LED led_12 (.in(opcs));
  LED led_13 (.in(ipc));
  LED led_14 (.in(ipcs));
  LED led_15 (.in(special));
  LED led_16 (.in(CLK));
  LED led_17 (.in(nxt));
  LED led_18 (.in(ConditionalFlag));
  LED RD (.in(om));
  LED WR (.in(im));
  DotMatrix #(.matrixcols(32), .matrixrows(8)) dotmatrix_1 (
    .col0(multireg_1_out_7), .col1(multireg_1_out_8), .col2(multireg_1_out_9), .col3(multireg_1_out_10),
    .col4(multireg_1_out_11), .col5(multireg_1_out_12), .col6(multireg_1_out_13), .col7(multireg_1_out_14),
    .col8(multireg_1_out_15), .col9(multireg_1_out_16), .col10(multireg_1_out_17), .col11(multireg_1_out_18),
    .col12(multireg_1_out_19), .col13(multireg_1_out_20), .col14(multireg_1_out_21),
    .col15(multireg_1_out_22), .col16(multireg_1_out_23), .col17(multireg_1_out_24),
    .col18(multireg_1_out_25), .col19(multireg_1_out_26), .col20(multireg_1_out_27),
    .col21(multireg_1_out_28), .col22(multireg_1_out_29), .col23(multireg_1_out_30),
    .col24(multireg_1_out_31), .col25(multireg_1_out_32), .col26(multireg_1_out_33),
    .col27(multireg_1_out_34), .col28(multireg_1_out_35), .col29(multireg_1_out_36),
    .col30(multireg_1_out_37), .col31(multireg_1_out_38));
  multireg multireg_1 (
    .RESET(in_2), .EN(or_2_out), .SEL(subtractor_1_out[4:0]), .CLK(and_7_out), .DATA(Databus),
    .out_7(multireg_1_out_7), .out_8(multireg_1_out_8), .out_9(multireg_1_out_9), .out_10(multireg_1_out_10),
    .out_11(multireg_1_out_11), .out_12(multireg_1_out_12), .out_13(multireg_1_out_13),
    .out_14(multireg_1_out_14), .out_15(multireg_1_out_15), .out_16(multireg_1_out_16),
    .out_17(multireg_1_out_17), .out_18(multireg_1_out_18), .out_19(multireg_1_out_19),
    .out_20(multireg_1_out_20), .out_21(multireg_1_out_21), .out_22(multireg_1_out_22),
    .out_23(multireg_1_out_23), .out_24(multireg_1_out_24), .out_25(multireg_1_out_25),
    .out_26(multireg_1_out_26), .out_27(multireg_1_out_27), .out_28(multireg_1_out_28),
    .out_29(multireg_1_out_29), .out_30(multireg_1_out_30), .out_31(multireg_1_out_31),
    .out_32(multireg_1_out_32), .out_33(multireg_1_out_33), .out_34(multireg_1_out_34),
    .out_35(multireg_1_out_35), .out_36(multireg_1_out_36), .out_37(multireg_1_out_37),
    .out_38(multireg_1_out_38));  // open: out_6
  S_R_Flip_Flop s_r_ff_1 (.reset(in_6), .Qn(s_r_ff_1_qn), .preset(in_4));  // open: S, R, clk, Q
  and and_6 (CLK, s_r_ff_1_qn, CLKIN);
  and and_7 (and_7_out, or_2_out, om, CLK);
  or or_3 (or_3_out, in_2, nxt);
  ROM rom_1 (.addr({Instruction, InstructionCounter}), .data({nxt, rom_1_data[6:4], special, rom_1_data[2:0]}));
  assign controlled_buffer_4_out = special ? Instruction : 4'bz;  // Controlled_Buffer controlled_buffer_4
  not not_4 (not_4_out, special);
  assign controlled_buffer_4_out = not_4_out ? Databus[3:0] : 4'bz;  // Controlled_Buffer controlled_buffer_5
  Counter #(.max('hf), .trigger("falling"), .width(4)) counter_1 (
    .clr(or_3_out), .load(1'b0), .up(1'b1), .count(1'b1), .clk(CLK), .Q(InstructionCounter));  // open: D, carry
  Register PrimaryBuffer (
    .D({Databus[7:4], controlled_buffer_4_out}), .en(ipb), .clk(CLK), .Q({Instruction, Condition}));  // open: clr
  Register u_SecondaryBuffer (.D(Databus), .en(isb), .clk(CLK), .Q(SecondaryBuffer));  // open: clr
  assign {Databus12, Databus} = osb ? {Condition, SecondaryBuffer} : 12'bz;  // Controlled_Buffer controlled_buffer_6
  assign Databus = osb ? SecondaryBuffer : 8'bz;  // Controlled_Buffer controlled_buffer_7
  Demultiplexer #(.select(3)) demultiplexer_1 (
    .out1(im), .out2(ipb), .out3(isb), .out4(ia), .out5(ialu), .out6(ipc), .out7(ipcs), .in(1'b1),
    .sel(rom_1_data[2:0]));  // open: out0
  Demultiplexer #(.select(3)) demultiplexer_2 (
    .out1(om), .out2(opb), .out3(osb), .out4(oa), .out5(oalu), .out6(opc), .out7(opcs), .in(1'b1),
    .sel(rom_1_data[6:4]));  // open: out0
  Register u_Accumulator (.D(Databus), .en(ia), .clk(CLK), .Q(Accumulator));  // open: clr
  Register ALUbuffer (.D(ALUin), .en(ialu), .clk(CLK), .Q(ALU));  // open: clr
  assign Databus = oa ? Accumulator : 8'bz;  // Controlled_Buffer controlled_buffer_8
  assign Databus = oalu ? ALU : 8'bz;  // Controlled_Buffer controlled_buffer_9
  Adder adder_1 (.a(Accumulator), .b(Databus), .out(adder_1_out), .cin(ConditionalFlag), .cout(Carry));
  assign nand_1_out = ~(Accumulator & Databus);  // NAND_Gate nand_1, 8 bits wide
  and and_8 (ucf, ialu, special);
  not not_5 (not_5_out, Instruction[3]);
  not not_6 (not_6_out, Condition[0]);
  and and_9 (and_9_out, not_5_out, Condition[0], Instruction[0]);
  and and_10 (and_10_out, not_5_out, not_6_out, Instruction[0]);
  assign ALUin = and_10_out ? {Accumulator[6:0], ConditionalFlag} : 8'bz;  // Controlled_Buffer controlled_buffer_10
  assign ALUin = and_9_out ? {ConditionalFlag, Accumulator[7:1]} : 8'bz;  // Controlled_Buffer controlled_buffer_11
  and and_11 (and_11_out, Instruction[3], Instruction[0]);
  not not_7 (not_7_out, Instruction[0]);
  assign ALUin = and_11_out ? nand_1_out : 8'bz;  // Controlled_Buffer controlled_buffer_12
  _74138 #(.ShowInternalStructure("true")) u_74138_1 (
    .pin1(Condition[1]), .pin2(Condition[2]), .pin3(Condition[3]), .pin4(n74138_1_pin4),
    .pin5(n74138_1_pin5), .pin6(n74138_1_pin6), .pin7(n74138_1_pin7), .pin15(n74138_1_pin15),
    .pin14(n74138_1_pin14), .pin13(n74138_1_pin13), .pin12(n74138_1_pin12), .pin11(n74138_1_pin11),
    .pin10(n74138_1_pin10), .pin9(n74138_1_pin9));
  not not_8 (not_8_out, n74138_1_pin15);
  Pull_Resistor pull_resistor_3 (.node(pull_resistor_3_node));
  assign controlled_buffer_13_out = not_8_out ? pull_resistor_3_node : 1'bz;  // Controlled_Buffer controlled_buffer_13
  not not_9 (not_9_out, n74138_1_pin14);
  assign ALUin = not_7_out ? adder_1_out : 8'bz;  // Controlled_Buffer controlled_buffer_14
  assign controlled_buffer_15_out = not_9_out ? Equal : 1'bz;  // Controlled_Buffer controlled_buffer_15
  not not_10 (not_10_out, n74138_1_pin13);
  assign controlled_buffer_16_out = not_10_out ? LessThan : 1'bz;  // Controlled_Buffer controlled_buffer_16
  not not_11 (not_11_out, n74138_1_pin12);
  assign controlled_buffer_17_out = not_11_out ? GreaterThan : 1'bz;  // Controlled_Buffer controlled_buffer_17
  not not_12 (not_12_out, n74138_1_pin11);
  assign controlled_buffer_18_out = not_12_out ? Device0 : 1'bz;  // Controlled_Buffer controlled_buffer_18
  not not_13 (not_13_out, n74138_1_pin10);
  assign not_14_out = ~Accumulator;  // NOT_Gate not_14, 8 bits wide
  assign controlled_buffer_19_out = not_13_out ? Device1 : 1'bz;  // Controlled_Buffer controlled_buffer_19
  not not_15 (not_15_out, n74138_1_pin9);
  assign controlled_buffer_20_out = not_15_out ? Device2 : 1'bz;  // Controlled_Buffer controlled_buffer_20
  not not_16 (not_16_out, n74138_1_pin7);
  assign controlled_buffer_21_out = not_16_out ? Device3 : 1'bz;  // Controlled_Buffer controlled_buffer_21
  Pull_Resistor #(.pull(1)) pull_resistor_4 (.node(pull_resistor_4_node));
  Adder adder_2 (.a(Databus), .b(not_14_out), .out(adder_2_out), .cin(pull_resistor_4_node), .cout(adder_2_cout));
  assign controlled_buffer_22_out = not_17_out ? Carry : 1'bz;  // Controlled_Buffer controlled_buffer_22
  not not_17 (not_17_out, ucf);
  assign controlled_buffer_22_out = ucf ? ConditionalResult : 1'bz;  // Controlled_Buffer controlled_buffer_23
  Pull_Resistor pull_resistor_5 (.node(controlled_buffer_13_out));
  Pull_Resistor pull_resistor_6 (.node(controlled_buffer_15_out));
  Pull_Resistor pull_resistor_7 (.node(controlled_buffer_16_out));
  Pull_Resistor pull_resistor_8 (.node(controlled_buffer_17_out));
  Pull_Resistor pull_resistor_9 (.node(controlled_buffer_18_out));
  Pull_Resistor pull_resistor_10 (.node(controlled_buffer_19_out));
  Pull_Resistor pull_resistor_11 (.node(controlled_buffer_20_out));
  Pull_Resistor pull_resistor_12 (.node(controlled_buffer_21_out));
  nor nor_1 (nor_1_out, adder_2_out[0], adder_2_out[1], adder_2_out[2], adder_2_out[3], adder_2_out[4], adder_2_out[5], adder_2_out[6], adder_2_out[7]);
  not not_18 (not_18_out, nor_1_out);
  and and_12 (Equal, nor_1_out, adder_2_cout);
  and and_13 (LessThan, adder_2_cout, not_18_out);
  nor nor_2 (GreaterThan, Equal, LessThan);
  Register #(.width(1)) register_1 (
    .D(controlled_buffer_22_out), .en(ialu), .clk(CLK), .Q(ConditionalFlag));  // open: clr
  or or_4 (or_4_out, controlled_buffer_13_out, controlled_buffer_15_out, controlled_buffer_16_out, controlled_buffer_17_out, controlled_buffer_18_out, controlled_buffer_19_out, controlled_buffer_20_out, controlled_buffer_21_out);
  not not_19 (not_19_out, or_4_out);
  assign ConditionalResult = and_14_out ? or_4_out : 1'bz;  // Controlled_Buffer controlled_buffer_24
  and and_14 (and_14_out, ucf, not_20_out);
  and and_15 (and_15_out, ucf, Condition[0]);
  assign ConditionalResult = and_15_out ? not_19_out : 1'bz;  // Controlled_Buffer controlled_buffer_25
  Pull_Resistor pull_resistor_13 (.node(ConditionalResult));
  not not_20 (not_20_out, Condition[0]);
  // also tied to GND on the sheet: {n74138_1_pin4, n74138_1_pin5}
  // also tied to VCC on the sheet: n74138_1_pin6

  // Other names for the same wires on the sheet: Databus12[7:0] = Databus; Memory[7:0] = Databus; Dev0 = Device0;
  //   Dev1 = Device1; Dev2 = Device2; Dev3 = Device3; HALT = in_4; PrimaryBuffer[7:0] = {Instruction, Condition};
  //   RES = in_6; RESET = in_2

  // Notes on the sheet:
  //   contents of rom_1 (hex, n*v repeats v):
  //   12 e 14 e 80 11*0 12 e 13 e 67 36 41 76 80 7*0 12 e 13 e 35 54 80 9*0 12 e 5 54 80 11*0 12 e 1d e 80
  //   11*0 12 e e 80 12*0 12 e 13 36 80 11*0 12 e 13 e 36 80 10*0 12 e 13 e 67 36 14 76 80 7*0 12 e 13 e
  //   67 36 1a e 13 36 41 76 80 0 0 0 12 e 13 e 67 36 13 35 54 76 80 5*0 12 e 13 e 13 35 54 80 8*0 12 5d e
  //   80 12*0 12 e 13 e 67 36 71 e f1 76 80 5*0 12 e 13 67 26 1a e 13 36 80 6*0 12 e 13 67 26 1a e 13 36
  //   80
  //   SL
  //   SR
  //   This is basically a Multiplexer
endmodule
